# Fritzing sketch VU.PCB (saved by Fritzing 0.9.3b)
circuit board: 5cm x 5cm
breadboards: 1

parts:
  Power = Header 2 [package=screwterminal-3.5mm-2_lock]
  10k_pot = Header 3 [package=screwterminal-3.5mm-3_lock.007s]
  Switch = Header 4 [package=screwterminal-3.5mm-4_lock]
  MAX4466 = Header 3 [package=screwterminal-3.5mm-3_lock.007s]
  WS2812B = Header 3 [package=screwterminal-3.5mm-3_lock.007s]
  10k_pot_2 = Header 3 [package=screwterminal-3.5mm-3_lock.007s]
  10k = Resistor [tolerance=±5% resistance=10k package=THT]
  Arduino_Nano = Arduino Nano (Rev3.0) (ICSP)

nets:
  N1: Power.1, 10k_pot.1, Switch.3, WS2812B.1, 10k_pot_2.1, Arduino_Nano.5V
  N2: Power.2, 10k_pot.3, MAX4466.2, WS2812B.3, 10k_pot_2.3, 10k.Pin_1, Arduino_Nano.GND
  N3: 10k_pot.2, Arduino_Nano.A0
  N4: Switch.2, Arduino_Nano.D3
  N5: Switch.4, 10k.Pin_0
  N6: MAX4466.1, Arduino_Nano.A4
  N7: MAX4466.3, Arduino_Nano.AREF, Arduino_Nano.3V3
  N8: WS2812B.2, Arduino_Nano.D6
  N9: 10k_pot_2.2, Arduino_Nano.A1

notes:
  GND
  D6
  +5V
  OUT
  VCC
  R1
  A1
  D3
  A0
  A4
  AREF
  3V3
  B
